// Logisim project noughts_and_crosses.circ as structural Verilog: 3 circuits, main circuit main
module main (
  input  [23:0] in_1
);

  wire [1:0] dis0, dis1, dis2, dis3, dis4, dis5, dis6, dis7, dis8;
  wire [2:0] led_controller_1_out_2, led_controller_1_out_3, led_controller_1_out_4, led_controller_2_out_2,
       led_controller_2_out_3, led_controller_2_out_4, led_controller_3_out_2, led_controller_3_out_3,
       led_controller_3_out_4, led_controller_4_out_2, led_controller_4_out_3, led_controller_4_out_4,
       led_controller_5_out_2, led_controller_5_out_3, led_controller_5_out_4, led_controller_6_out_2,
       led_controller_6_out_3, led_controller_6_out_4, led_controller_7_out_2, led_controller_7_out_3,
       led_controller_7_out_4, led_controller_8_out_2, led_controller_8_out_3, led_controller_8_out_4,
       led_controller_9_out_2, led_controller_9_out_3, led_controller_9_out_4;

  // CdM_8_mark5 cdm_8_mark5_1: pin names not known
  game_status_controller game_status_controller_1 (
    .in_1(in_1), .out_2(dis0), .out_3(dis1), .out_4(dis2), .out_5(dis3), .out_6(dis4), .out_7(dis5),
    .out_8(dis6), .out_9(dis7), .out_10(dis8));
  led_controller led_controller_1 (
    .in_1(dis0), .out_2(led_controller_1_out_2), .out_3(led_controller_1_out_3),
    .out_4(led_controller_1_out_4));
  DotMatrix #(.matrixcols(3), .matrixrows(3)) dotmatrix_1 (
    .col0(led_controller_1_out_2), .col1(led_controller_1_out_3), .col2(led_controller_1_out_4));
  Button button_1 ();  // open: out
  DotMatrix #(.matrixcols(3), .matrixrows(3)) dotmatrix_2 (
    .col0(led_controller_2_out_2), .col1(led_controller_2_out_3), .col2(led_controller_2_out_4));
  led_controller led_controller_2 (
    .in_1(dis3), .out_2(led_controller_2_out_2), .out_3(led_controller_2_out_3),
    .out_4(led_controller_2_out_4));
  Button button_2 ();  // open: out
  DotMatrix #(.matrixcols(3), .matrixrows(3)) dotmatrix_3 (
    .col0(led_controller_3_out_2), .col1(led_controller_3_out_3), .col2(led_controller_3_out_4));
  led_controller led_controller_3 (
    .in_1(dis6), .out_2(led_controller_3_out_2), .out_3(led_controller_3_out_3),
    .out_4(led_controller_3_out_4));
  Button button_3 ();  // open: out
  DotMatrix #(.matrixcols(3), .matrixrows(3)) dotmatrix_4 (
    .col0(led_controller_4_out_2), .col1(led_controller_4_out_3), .col2(led_controller_4_out_4));
  led_controller led_controller_4 (
    .in_1(dis1), .out_2(led_controller_4_out_2), .out_3(led_controller_4_out_3),
    .out_4(led_controller_4_out_4));
  Button button_4 ();  // open: out
  DotMatrix #(.matrixcols(3), .matrixrows(3)) dotmatrix_5 (
    .col0(led_controller_5_out_2), .col1(led_controller_5_out_3), .col2(led_controller_5_out_4));
  led_controller led_controller_5 (
    .in_1(dis4), .out_2(led_controller_5_out_2), .out_3(led_controller_5_out_3),
    .out_4(led_controller_5_out_4));
  Button button_5 ();  // open: out
  led_controller led_controller_6 (
    .in_1(dis7), .out_2(led_controller_6_out_2), .out_3(led_controller_6_out_3),
    .out_4(led_controller_6_out_4));
  DotMatrix #(.matrixcols(3), .matrixrows(3)) dotmatrix_6 (
    .col0(led_controller_6_out_2), .col1(led_controller_6_out_3), .col2(led_controller_6_out_4));
  Button button_6 ();  // open: out
  led_controller led_controller_7 (
    .in_1(dis2), .out_2(led_controller_7_out_2), .out_3(led_controller_7_out_3),
    .out_4(led_controller_7_out_4));
  DotMatrix #(.matrixcols(3), .matrixrows(3)) dotmatrix_7 (
    .col0(led_controller_7_out_2), .col1(led_controller_7_out_3), .col2(led_controller_7_out_4));
  Button button_7 ();  // open: out
  DotMatrix #(.matrixcols(3), .matrixrows(3)) dotmatrix_8 (
    .col0(led_controller_8_out_2), .col1(led_controller_8_out_3), .col2(led_controller_8_out_4));
  led_controller led_controller_8 (
    .in_1(dis5), .out_2(led_controller_8_out_2), .out_3(led_controller_8_out_3),
    .out_4(led_controller_8_out_4));
  Button button_8 ();  // open: out
  led_controller led_controller_9 (
    .in_1(dis8), .out_2(led_controller_9_out_2), .out_3(led_controller_9_out_3),
    .out_4(led_controller_9_out_4));
  DotMatrix #(.matrixcols(3), .matrixrows(3)) dotmatrix_9 (
    .col0(led_controller_9_out_2), .col1(led_controller_9_out_3), .col2(led_controller_9_out_4));
  Button button_9 ();  // open: out
endmodule

module led_controller (
  input  [1:0] in_1,
  output [2:0] out_2,
  output [2:0] out_3,
  output [2:0] out_4
);

  wire not_1_out;
  wire [8:0] multiplexer_1_out;

  Multiplexer #(.width(9), .enable("false")) multiplexer_1 (
    .in0(9'h1ef), .in1(9'h155), .out(multiplexer_1_out), .sel(in_1[0]));
  not not_1 (not_1_out, in_1[1]);
  Multiplexer #(.width(9), .enable("false")) multiplexer_2 (
    .in0(multiplexer_1_out), .in1({9{1'b0}}), .out({out_4, out_3, out_2}), .sel(not_1_out));
endmodule

module game_status_controller (
  input  [23:0] in_1,
  output [1:0] out_2,
  output [1:0] out_3,
  output [1:0] out_4,
  output [1:0] out_5,
  output [1:0] out_6,
  output [1:0] out_7,
  output [1:0] out_8,
  output [1:0] out_9,
  output [1:0] out_10
);


  assign out_2 = in_1[23:22];
  assign out_3 = in_1[21:20];
  assign out_4 = in_1[19:18];
  assign out_5 = in_1[17:16];
  assign out_6 = in_1[15:14];
  assign out_7 = in_1[13:12];
  assign out_8 = in_1[11:10];
  assign out_9 = in_1[9:8];
  assign out_10 = in_1[7:6];
endmodule
